# Fritzing sketch sketch (saved by Fritzing 0.9.3b)

parts:
  MCU1 = Raspberry Pi Zero
  S1 = H-Bridge with L298N
  M1 = DC Motor
  M2 = DC Motor

nets:
  N1: MCU1.pin_6, MCU1.pin_14, S1.GND
  N2: MCU1.pin_7, S1.IN1
  N3: MCU1.pin_11, S1.IN2
  N4: MCU1.pin_13, S1.IN3
  N5: MCU1.pin_15, S1.IN4
  N6: S1.OUT3-Motor2, M1.pin_2, M2.pin_1
  N7: S1.OUT4-Motor2, M1.pin_1, M2.pin_2

custom parts:
  H-Bridge with L298N: h-bridge
